# Fritzing sketch blinkingLEDAdvanced (saved by Fritzing 0.7.11b)
breadboards: 1

parts:
  S1 = Pushbutton [package=THT]
  R1 = Resistor [tolerance=±5% resistance=220 package=THT]
  LED1 = LED - 5mm [color="Red (633nm)" package="5 mm [THT]"]
  Arduino2 = Arduino

nets:
  N1: S1.leg0, R1.Pin_0, Arduino2.D10
  N2: S1.leg1, Arduino2.+5V
  N3: R1.Pin_1, LED1.cathode, Arduino2.GND
  N4: LED1.anode, Arduino2.D11
