# Fritzing sketch doorbellBuzzer (saved by Fritzing 0.7.11b)
breadboards: 1

parts:
  Arduino1 = Arduino
  Part1 = XBee Explorer Regulated
  J1 = Piezo Speaker

nets:
  N1: Arduino1.D5, J1.pin2
  N2: Arduino1.D1TX, Part1.DIN
  N3: Arduino1.D0RX, Part1.DOUT
  3V3: Arduino1.3V3, Part1.3.3V
  GND: Arduino1.GND, Part1.GND, J1.pin1
