# Fritzing sketch doorbellSwitch (saved by Fritzing 0.7.11b)
breadboards: 1

parts:
  Arduino1 = Arduino
  Part1 = XBee Explorer Regulated
  S1 = Pushbutton [package=THT]
  R1 = 10k Ω Resistor [package=THT]

nets:
  N1: Arduino1.D2, S1.leg1, R1.Pin_0
  N2: Arduino1.D1TX, Part1.DIN
  N3: Arduino1.D0RX, Part1.DOUT
  3V3: Arduino1.3V3, Part1.3.3V, S1.leg0
  GND: Arduino1.GND, Part1.GND, R1.Pin_1
