# Fritzing sketch sunset_detector (saved by Fritzing 0.7.12b)
breadboards: 1

parts:
  Part2 = XBee Explorer Regulated
  Part3 = XBee Explorer Regulated
  Arduino1 = Arduino
  R1 = Resistor [tolerance=±5% resistance=20k package=THT]
  R2 = Photocell (LDR) [package=THT]
  LED1 = LED - 5mm [color="Blue (505nm)" package="5 mm [THT]"]
  LED2 = LED - 5mm [color="Red (633nm)" package="5 mm [THT]"]
  LED3 = LED - 5mm [color="White (4500K)" package="5 mm [THT]"]

nets:
  GND: Part2.GND, Part3.GND, Arduino1.GND, R2.pin_0, LED1.cathode, LED2.cathode, LED3.cathode
  3.3V: Part2.3.3V, Part3.3.3V, Arduino1.3V3, R1.Pin_1
  N1: Part2.DIO0, R1.Pin_0, R2.pin_1
  N2: Part3.DIN, Arduino1.D1TX
  N3: Part3.DOUT, Arduino1.D0RX
  N4: Arduino1.D12, LED3.anode
  N5: Arduino1.D11, LED2.anode
  N6: Arduino1.D10, LED1.anode
